// Digital circuit 4bit_ALU.dig as structural Verilog
module _4bit_ALU (
  input  [3:0] A,
  input  [3:0] B,
  input  [2:0] control_signal,
  input  Cin,
  input  [3:0] placeholder,
  input  cinAdd,
  output [3:0] Output,
  output Zero_Flag,
  output Slt_Flag
);

  wire [3:0] _4bit_full_adder_1_s, _4bit_subtractor_1_sub, and_1_out, or_1_out, slt_func_1_reuslt, xor_1_out;

  _4bit_full_adder _4bit_full_adder_1 (.A(A), .B(B), .Cin(cinAdd), .S(_4bit_full_adder_1_s));  // open: C
  _4bit_subtractor _4bit_subtractor_1 (.A(A), .B(B), .Cin(Cin), .Sub(_4bit_subtractor_1_sub));  // open: C
  SLT_Func slt_func_1 (.A(A), .B(B), .Cin(Cin), .Reuslt(slt_func_1_reuslt));  // open: MSb
  assign and_1_out = A & B;  // And and_1, 4 bits wide
  assign or_1_out = A | B;  // Or or_1, 4 bits wide
  assign xor_1_out = A ^ B;  // XOr xor_1, 4 bits wide
  Multiplexer #(.Selector_Bits(3), .Bits(4)) multiplexer_1 (
    .sel(control_signal), .in_0(_4bit_full_adder_1_s), .in_1(_4bit_subtractor_1_sub),
    .in_2(slt_func_1_reuslt), .in_3(and_1_out), .in_4(or_1_out), .in_5(xor_1_out), .in_6(placeholder),
    .in_7(placeholder), .out(Output));
  nor nor_1 (Zero_Flag, Output[0], Output[1], Output[2], Output[3]);

  assign Slt_Flag = Output[3];

  // Notes on the sheet:
  //   Cin: default 1
endmodule
