// Digital circuit 4bit_CPU.dig as structural Verilog
module _4bit_CPU (
  input  clk,
  input  Enable_F_D_E,
  input  ZeroFlag1,
  input  [3:0] clear2,
  input  ZeroFlag2,
  input  [3:0] Clear1,
  input  [3:0] Data,
  input  [3:0] Constant,
  input  [3:0] in_9,
  output [3:0] ReadReg1,
  output [3:0] ALU_OUTPUT,
  output [3:0] Read_REg2
);

  wire controlunit_1_il, controlunit_1_instruction_fetch, controlunit_1_pcincrement, controlunit_1_rr1,
       controlunit_1_rr2, controlunit_1_we, controlunit_1_wr;
  wire [2:0] controlunit_1_alu;
  wire [3:0] Counter_output, ir_1_instruction, multiplexer_1_out, ramblock_1_read_output;

  ProgramCounter Counter (
    .Clock(clk), .constant(Constant), .cin(1'b1), .Selector(controlunit_1_pcincrement),
    .\output (Counter_output));
  ramBlock ramblock_1 (
    .Write_Address(Counter_output), .Data(Data), .Read_Address(Counter_output), .Clock(clk),
    .Read_Output(ramblock_1_read_output));
  IR ir_1 (
    .Data(ramblock_1_read_output), .Clock(clk), .Enable(controlunit_1_instruction_fetch),
    .Instruction(ir_1_instruction));
  ControlUnit controlunit_1 (
    .\input (ir_1_instruction), .En(Enable_F_D_E), .clock(clk), .RR1(controlunit_1_rr1),
    .RR2(controlunit_1_rr2), .WR(controlunit_1_wr), .WE(controlunit_1_we), .IL(controlunit_1_il),
    .Alu(controlunit_1_alu), .PCIncrement(controlunit_1_pcincrement),
    .Instruction_Fetch(controlunit_1_instruction_fetch));
  RegisterFile registerfile_1 (
    .Clock(clk), .Clear1(Clear1), .Zero_Flag1(ZeroFlag1), .Clear2(clear2), .Zero_Flag2(ZeroFlag2),
    .Write_Register(controlunit_1_wr), .Write_Data(multiplexer_1_out), .Read_Reg1(controlunit_1_rr1),
    .Read_Reg2(controlunit_1_rr2), .Write_Enable(controlunit_1_we), .R1(ReadReg1), .R2(Read_REg2));
  _4bit_ALU _4bit_alu_1 (
    .A(ReadReg1), .B(Read_REg2), .control_signal(controlunit_1_alu), .Cin(1'b1), .placeholder(in_9),
    .cinAdd(1'b1), .Output(ALU_OUTPUT));  // open: Zero_Flag, Slt_Flag
  Multiplexer #(.Bits(4)) multiplexer_1 (
    .sel(controlunit_1_il), .in_0(ALU_OUTPUT), .in_1(ramblock_1_read_output), .out(multiplexer_1_out));

  // Notes on the sheet:
  //   Constant: default 1
endmodule
