// Digital circuit 4bit_full_adder.dig as structural Verilog
module _4bit_full_adder (
  input  [3:0] A,
  input  [3:0] B,
  input  Cin,
  output [3:0] S,
  output C
);

  wire _1bit_full_adder_1_cout, _1bit_full_adder_2_cout, _1bit_full_adder_3_cout;

  _1bit_Full_Adder _1bit_full_adder_1 (.A(A[0]), .B(B[0]), .Cin(Cin), .Sum(S[0]), .Cout(_1bit_full_adder_1_cout));
  _1bit_Full_Adder _1bit_full_adder_2 (
    .A(A[1]), .B(B[1]), .Cin(_1bit_full_adder_1_cout), .Sum(S[1]), .Cout(_1bit_full_adder_2_cout));
  _1bit_Full_Adder _1bit_full_adder_3 (
    .A(A[2]), .B(B[2]), .Cin(_1bit_full_adder_2_cout), .Sum(S[2]), .Cout(_1bit_full_adder_3_cout));
  _1bit_Full_Adder _1bit_full_adder_4 (.A(A[3]), .B(B[3]), .Cin(_1bit_full_adder_3_cout), .Sum(S[3]), .Cout(C));
endmodule
