// Digital circuit 4bit_subtractor.dig as structural Verilog
module _4bit_subtractor (
  input  [3:0] A,
  input  [3:0] B,
  input  Cin,
  output [3:0] Sub,
  output C
);

  wire [3:0] not_1_out;

  assign not_1_out = ~B;  // Not not_1, 4 bits wide
  _4bit_full_adder _4bit_full_adder_1 (.A(A), .B(not_1_out), .Cin(Cin), .S(Sub), .C(C));

  // Notes on the sheet:
  //   Cin: default 1
endmodule
