// Digital circuit ControlUnit.dig as structural Verilog
module ControlUnit (
  input  [3:0] \input ,
  input  En,
  input  clock,
  output RR1,
  output RR2,
  output WR,
  output WE,
  output IL,
  output [2:0] Alu,
  output PCIncrement,
  output Instruction_Fetch
);

  wire and_1_out, and_2_out, and_3_out, and_4_out, and_5_out, and_6_out, and_7_out, and_8_out, and_10_out,
       d_ff_1_q, d_ff_2_q, not_1_out, not_2_out, not_3_out, not_4_out, not_5_out, not_6_out, not_7_out,
       not_8_out, not_9_out, not_10_out, not_11_out, not_12_out, not_13_out, or_1_out, or_2_out, or_5_out;

  and and_1 (and_1_out, d_ff_1_q, not_1_out);
  not not_1 (not_1_out, En);
  and and_2 (and_2_out, En, d_ff_2_q);
  and and_3 (and_3_out, not_2_out, not_3_out, \input [1]);
  not not_2 (not_2_out, \input [3]);
  not not_3 (not_3_out, \input [2]);
  and and_4 (and_4_out, not_4_out, not_5_out, not_6_out);
  not not_4 (not_4_out, \input [2]);
  not not_5 (not_5_out, \input [1]);
  not not_6 (not_6_out, \input [0]);
  or or_1 (or_1_out, \input [3], \input [1], \input [0]);
  and and_5 (and_5_out, not_7_out, not_8_out, \input [0]);
  not not_7 (not_7_out, \input [3]);
  not not_8 (not_8_out, \input [1]);
  and and_6 (and_6_out, not_9_out, \input [1], not_10_out);
  not not_9 (not_9_out, \input [3]);
  not not_10 (not_10_out, \input [0]);
  or or_2 (or_2_out, and_1_out, and_2_out);
  or or_3 (WR, and_3_out, and_4_out);
  or or_4 (IL, and_5_out, and_6_out);
  and and_7 (and_7_out, not_11_out, d_ff_2_q);
  not not_11 (not_11_out, En);
  and and_8 (and_8_out, not_12_out, not_13_out, En);
  not not_12 (not_12_out, d_ff_1_q);
  not not_13 (not_13_out, d_ff_2_q);
  Multiplexer #(.Selector_Bits(4), .Bits(3)) multiplexer_1 (
    .sel(\input ), .in_0(3'b111), .in_1(3'b111), .in_2(3'b111), .in_3(3'b111), .in_4(3'b111), .in_5(3'b111),
    .in_6(3'b111), .in_7(3'b111), .in_8(3'b111), .in_9(3'b000), .in_10(3'b001), .in_11(3'b010),
    .in_12(3'b011), .in_13(3'b100), .in_14(3'b101), .in_15(3'b111), .out(Alu));
  or or_5 (or_5_out, and_7_out, and_8_out);
  D_FF d_ff_1 (.D(or_2_out), .C(clock), .Q(d_ff_1_q));  // open: nQ
  and and_9 (WE, or_1_out, d_ff_1_q);
  D_FF d_ff_2 (.D(or_5_out), .C(clock), .Q(d_ff_2_q));  // open: nQ
  and and_10 (and_10_out, IL, d_ff_2_q);
  nor nor_1 (Instruction_Fetch, d_ff_1_q, d_ff_2_q);
  or or_6 (PCIncrement, d_ff_1_q, and_10_out);

  assign RR1 = \input [3];
  assign RR2 = 1'b1;
endmodule
