// Digital circuit FailingSequential.dig as structural Verilog
module FailingSequential (
  input  x,
  input  clk,
  output out_2
);

  wire and_1_out, and_2_out, and_3_out, and_4_out, and_5_out, d_ff_1_nq, d_ff_1_q, d_ff_2_q, not_1_out,
       or_1_out;

  not not_1 (not_1_out, x);
  and and_1 (and_1_out, d_ff_1_q, x);
  and and_2 (and_2_out, x, d_ff_2_q);
  and and_3 (and_3_out, d_ff_1_q, not_1_out);
  and and_4 (and_4_out, d_ff_2_q, not_1_out);
  or or_1 (or_1_out, and_1_out, and_2_out);
  or or_2 (out_2, and_3_out, and_4_out);
  and and_5 (and_5_out, d_ff_1_nq, x);
  D_FF d_ff_1 (.D(or_1_out), .C(clk), .Q(d_ff_1_q), .nQ(d_ff_1_nq));
  D_FF d_ff_2 (.D(and_5_out), .C(clk), .Q(d_ff_2_q));  // open: nQ
endmodule
