// Digital circuit IR.dig as structural Verilog
module IR (
  input  [3:0] Data,
  input  Clock,
  input  Enable,
  output [3:0] Instruction
);

  wire [3:0] multiplexer_1_out;

  Multiplexer #(.Bits(4)) multiplexer_1 (.sel(Enable), .in_0(Data), .in_1(Instruction), .out(multiplexer_1_out));
  Register register_1 (.Clock(Clock), .Input(multiplexer_1_out), .Output(Instruction));
endmodule
