// Digital circuit ProgramCounter.dig as structural Verilog
module ProgramCounter (
  input  Clock,
  input  [3:0] constant,
  input  cin,
  input  Selector,
  output [3:0] \output 
);

  wire [3:0] _4bit_full_adder_1_s, multiplexer_1_out;

  Multiplexer #(.Bits(4)) multiplexer_1 (
    .sel(Selector), .in_0(\output ), .in_1(_4bit_full_adder_1_s), .out(multiplexer_1_out));
  Register register_1 (.Clock(Clock), .Input(multiplexer_1_out), .Output(\output ));
  _4bit_full_adder _4bit_full_adder_1 (.A(\output ), .B(constant), .Cin(cin), .S(_4bit_full_adder_1_s));  // open: C

  // Notes on the sheet:
  //   constant: default 1
endmodule
