// Digital circuit RegisterFile.dig as structural Verilog
module RegisterFile (
  input  Clock,
  input  [3:0] Clear1,
  input  Zero_Flag1,
  input  [3:0] Clear2,
  input  Zero_Flag2,
  input  Write_Register,
  input  [3:0] Write_Data,
  input  Read_Reg1,
  input  Read_Reg2,
  input  Write_Enable,
  output [3:0] R1,
  output [3:0] R2
);

  wire demultiplexer_2_out_0, demultiplexer_2_out_1;
  wire [3:0] A_q, and_1_out, and_2_out, B_q, demultiplexer_1_out_0, demultiplexer_1_out_1, multiplexer_1_out,
       multiplexer_2_out;

  Demultiplexer #(.Bits(4)) demultiplexer_1 (
    .sel(Write_Register), .in(Write_Data), .out_0(demultiplexer_1_out_0), .out_1(demultiplexer_1_out_1));
  Demultiplexer demultiplexer_2 (
    .sel(Write_Register), .in(Write_Enable), .out_0(demultiplexer_2_out_0), .out_1(demultiplexer_2_out_1));
  assign and_1_out = demultiplexer_1_out_0 & multiplexer_1_out;  // And and_1, 4 bits wide
  assign and_2_out = demultiplexer_1_out_1 & multiplexer_2_out;  // And and_2, 4 bits wide
  Multiplexer #(.Bits(4)) multiplexer_1 (
    .sel(Zero_Flag1), .in_0(demultiplexer_1_out_0), .in_1(Clear1), .out(multiplexer_1_out));
  Multiplexer #(.Bits(4)) multiplexer_2 (
    .sel(Zero_Flag2), .in_0(demultiplexer_1_out_1), .in_1(Clear2), .out(multiplexer_2_out));
  Register #(.Bits(4)) A (.D(and_1_out), .C(Clock), .en(demultiplexer_2_out_0), .Q(A_q));
  Register #(.Bits(4)) B (.D(and_2_out), .C(Clock), .en(demultiplexer_2_out_1), .Q(B_q));
  Multiplexer #(.Bits(4)) multiplexer_3 (.sel(Read_Reg1), .in_0(A_q), .in_1(B_q), .out(R1));
  Multiplexer #(.Bits(4)) multiplexer_4 (.sel(Read_Reg2), .in_0(A_q), .in_1(B_q), .out(R2));
endmodule
