// Digital circuit SLT_Func.dig as structural Verilog
module SLT_Func (
  input  [3:0] A,
  input  [3:0] B,
  input  Cin,
  output MSb,
  output [3:0] Reuslt
);

  _4bit_subtractor _4bit_subtractor_1 (.A(A), .B(B), .Cin(Cin), .Sub(Reuslt), .C(MSb));
endmodule
