// Digital circuit ramBlock.dig as structural Verilog
module ramBlock (
  input  [3:0] Write_Address,
  input  [3:0] Data,
  input  [3:0] Read_Address,
  input  Clock,
  output [3:0] Read_Output
);

  wire [3:0] demultiplexer_1_out_0, demultiplexer_1_out_1, demultiplexer_1_out_2, demultiplexer_1_out_3,
       demultiplexer_1_out_4, demultiplexer_1_out_5, demultiplexer_1_out_6, demultiplexer_1_out_7,
       demultiplexer_1_out_8, demultiplexer_1_out_9, demultiplexer_1_out_10, demultiplexer_1_out_11,
       demultiplexer_1_out_12, demultiplexer_1_out_13, demultiplexer_1_out_14, demultiplexer_1_out_15,
       register_1_output, register_2_output, register_3_output, register_4_output, register_5_output,
       register_6_output, register_7_output, register_8_output, register_9_output, register_10_output,
       register_11_output, register_12_output, register_13_output, register_14_output, register_15_output,
       register_16_output;

  Demultiplexer #(.Selector_Bits(4), .Bits(4)) demultiplexer_1 (
    .sel(Write_Address), .in(Data), .out_0(demultiplexer_1_out_0), .out_1(demultiplexer_1_out_1),
    .out_2(demultiplexer_1_out_2), .out_3(demultiplexer_1_out_3), .out_4(demultiplexer_1_out_4),
    .out_5(demultiplexer_1_out_5), .out_6(demultiplexer_1_out_6), .out_7(demultiplexer_1_out_7),
    .out_8(demultiplexer_1_out_8), .out_9(demultiplexer_1_out_9), .out_10(demultiplexer_1_out_10),
    .out_11(demultiplexer_1_out_11), .out_12(demultiplexer_1_out_12), .out_13(demultiplexer_1_out_13),
    .out_14(demultiplexer_1_out_14), .out_15(demultiplexer_1_out_15));
  Register register_1 (.Clock(Clock), .Input(demultiplexer_1_out_0), .Output(register_1_output));
  Register register_2 (.Clock(Clock), .Input(demultiplexer_1_out_1), .Output(register_2_output));
  Register register_3 (.Clock(Clock), .Input(demultiplexer_1_out_2), .Output(register_3_output));
  Register register_4 (.Clock(Clock), .Input(demultiplexer_1_out_3), .Output(register_4_output));
  Register register_5 (.Clock(Clock), .Input(demultiplexer_1_out_4), .Output(register_5_output));
  Register register_6 (.Clock(Clock), .Input(demultiplexer_1_out_5), .Output(register_6_output));
  Register register_7 (.Clock(Clock), .Input(demultiplexer_1_out_6), .Output(register_7_output));
  Register register_8 (.Clock(Clock), .Input(demultiplexer_1_out_7), .Output(register_8_output));
  Register register_9 (.Clock(Clock), .Input(demultiplexer_1_out_8), .Output(register_9_output));
  Register register_10 (.Clock(Clock), .Input(demultiplexer_1_out_9), .Output(register_10_output));
  Register register_11 (.Clock(Clock), .Input(demultiplexer_1_out_10), .Output(register_11_output));
  Register register_12 (.Clock(Clock), .Input(demultiplexer_1_out_11), .Output(register_12_output));
  Register register_13 (.Clock(Clock), .Input(demultiplexer_1_out_12), .Output(register_13_output));
  Register register_14 (.Clock(Clock), .Input(demultiplexer_1_out_13), .Output(register_14_output));
  Register register_15 (.Clock(Clock), .Input(demultiplexer_1_out_14), .Output(register_15_output));
  Register register_16 (.Clock(Clock), .Input(demultiplexer_1_out_15), .Output(register_16_output));
  Multiplexer #(.Selector_Bits(4), .Bits(4)) multiplexer_1 (
    .sel(Read_Address), .in_0(register_1_output), .in_1(register_2_output), .in_2(register_3_output),
    .in_3(register_4_output), .in_4(register_5_output), .in_5(register_6_output), .in_6(register_7_output),
    .in_7(register_8_output), .in_8(register_9_output), .in_9(register_10_output),
    .in_10(register_11_output), .in_11(register_12_output), .in_12(register_13_output),
    .in_13(register_14_output), .in_14(register_15_output), .in_15(register_16_output), .out(Read_Output));
endmodule
